# Fritzing sketch version2 (saved by Fritzing 0.9.3b)
circuit board: 6.88566cm x 5.36311cm
circuit board: 5.51629cm x 5.35811cm
breadboards: 1

parts:
  Part1 = Arduino Uno (Rev3)
  R7 = Resistor [tolerance=±5% resistance=470 package=THT]
  R8 = Resistor [tolerance=±5% resistance=470 package=THT]
  R9 = Resistor [tolerance=±5% resistance=470 package=THT]
  LED1 = RGB LED (com. cathode, rgb) [package="5 mm [THT]"]
  LED2 = RGB LED (com. cathode, rgb) [package="5 mm [THT]"]
  LED3 = RGB LED (com. cathode, rgb) [package="5 mm [THT]"]
  R10 = Resistor [tolerance=±5% resistance=470 package=THT]
  LED4 = RGB LED (com. cathode, rgb) [package="5 mm [THT]"]
  LED5 = RGB LED (com. cathode, rgb) [package="5 mm [THT]"]
  LED6 = RGB LED (com. cathode, rgb) [package="5 mm [THT]"]
  R11 = Resistor [tolerance=±5% resistance=470 package=THT]
  LED7 = RGB LED (com. cathode, rgb) [package="5 mm [THT]"]
  LED8 = RGB LED (com. cathode, rgb) [package="5 mm [THT]"]
  LED9 = RGB LED (com. cathode, rgb) [package="5 mm [THT]"]
  R12 = Resistor [tolerance=±5% resistance=470 package=THT]
  R13 = Resistor [tolerance=±5% resistance=470 package=THT]
  R14 = Resistor [tolerance=±5% resistance=470 package=THT]
  R15 = Resistor [tolerance=±5% resistance=470 package=THT]
  J1 = female pin header, 5 pins [form="♀ (female)"]
  S1 = Pushbutton [package="[THT]"]
  S2 = Pushbutton [package="[THT]"]
  S3 = Pushbutton [package="[THT]"]
  J2 = female pin header, 5 pins [form="♀ (female)"]
  R16 = Resistor [tolerance=±5% resistance=4.7k package=THT]
  R19 = Resistor [tolerance=±5% resistance=2.2k package=THT]
  R20 = Resistor [tolerance=±5% resistance=10k package=THT]
  R21 = Resistor [tolerance=±5% resistance=100 package=THT]
  S4 = Pushbutton [package="[THT]"]
  S5 = Pushbutton [package="[THT]"]
  S6 = Pushbutton [package="[THT]"]
  R22 = Resistor [tolerance=±5% resistance=4.7k package=THT]
  R23 = Resistor [tolerance=±5% resistance=2.2k package=THT]
  R24 = Resistor [tolerance=±5% resistance=100 package=THT]
  R25 = Resistor [tolerance=±5% resistance=10k package=THT]
  S7 = Pushbutton [package="[THT]"]
  S8 = Pushbutton [package="[THT]"]
  S9 = Pushbutton [package="[THT]"]
  R26 = Resistor [tolerance=±5% resistance=10k package=THT]
  R27 = Resistor [tolerance=±5% resistance=100 package=THT]
  R28 = Resistor [tolerance=±5% resistance=2.2k package=THT]
  R29 = Resistor [tolerance=±5% resistance=4.7k package=THT]

nets:
  N1: Part1.A0, J1.pin3
  N2: Part1.A1, J1.pin4
  N3: Part1.A2, J1.pin5
  N4: Part1.D8, R8.Pin_0
  N5: Part1.D9_PWM, R9.Pin_0
  N6: Part1.D12/MISO, R7.Pin_0
  GND: Part1.GND, J1.pin2
  N7: Part1.D2, R15.Pin_0
  N8: Part1.D3_PWM, R13.Pin_0
  N9: Part1.D4, R11.Pin_0
  N10: Part1.D5_PWM, R14.Pin_0
  N11: Part1.D6_PWM, R12.Pin_0
  N12: Part1.D7, R10.Pin_0
  5V: Part1.5V, J1.pin1
  N13: R7.Pin_1, LED3.common_cathode
  N14: R8.Pin_1, LED1.common_cathode
  N15: R9.Pin_1, LED2.common_cathode
  N16: LED1.red_anode, LED2.red_anode, LED3.red_anode
  N17: LED1.green_anode, LED2.green_anode, LED3.green_anode
  N18: LED1.blue_anode, LED2.blue_anode, LED3.blue_anode
  N19: R10.Pin_1, LED5.common_cathode
  N20: LED4.red_anode, LED5.red_anode, LED6.red_anode
  N21: LED4.common_cathode, R14.Pin_1
  N22: LED4.green_anode, LED5.green_anode, LED6.green_anode
  N23: LED4.blue_anode, LED5.blue_anode, LED6.blue_anode
  N24: LED6.common_cathode, R12.Pin_1
  N25: R11.Pin_1, LED8.common_cathode
  N26: LED7.red_anode, LED8.red_anode, LED9.red_anode
  N27: LED7.common_cathode, R15.Pin_1
  N28: LED7.green_anode, LED8.green_anode, LED9.green_anode
  N29: LED7.blue_anode, LED8.blue_anode, LED9.blue_anode
  N30: LED9.common_cathode, R13.Pin_1
  N31: S1.Pin_1, S1.Pin_2, S2.Pin_1, S2.Pin_2, S3.Pin_1, S3.Pin_2, J2.pin3, R16.Pin_1
  N32: S1.Pin_3, S1.Pin_4, R20.Pin_0
  N33: S2.Pin_3, S2.Pin_4, R19.Pin_1
  N34: S3.Pin_3, S3.Pin_4, R21.Pin_1
  N35: J2.pin1, R16.Pin_0, R22.Pin_0, R29.Pin_0
  N36: J2.pin2, R19.Pin_0, R20.Pin_1, R21.Pin_0, R23.Pin_0, R24.Pin_0, R25.Pin_1, R26.Pin_1, R27.Pin_0, R28.Pin_0
  N37: J2.pin4, S4.Pin_1, S4.Pin_2, S5.Pin_1, S5.Pin_2, S6.Pin_1, S6.Pin_2, R22.Pin_1
  N38: J2.pin5, S7.Pin_1, S7.Pin_2, S8.Pin_1, S8.Pin_2, S9.Pin_1, S9.Pin_2, R29.Pin_1
  N39: S4.Pin_3, S4.Pin_4, R25.Pin_0
  N40: S5.Pin_3, S5.Pin_4, R23.Pin_1
  N41: S6.Pin_3, S6.Pin_4, R24.Pin_1
  N42: S7.Pin_3, S7.Pin_4, R27.Pin_1
  N43: S8.Pin_3, S8.Pin_4, R26.Pin_0
  N44: S9.Pin_3, S9.Pin_4, R28.Pin_1
